// Logisim project controlee.circ as structural Verilog: 1 circuit, main circuit main
module main (
  input  A__Op_3,
  input  B__Op_2,
  input  C__Op_1,
  input  D__Op_0,
  output write,
  output branch,
  output jump,
  output bnzi,
  output store,
  output load,
  output hibrido
);

  wire and_1_out, or_1_out;

  not not_1 (A__Op_3, A__Op_3);
  not not_2 (B__Op_2, B__Op_2);
  not not_3 (C__Op_1, C__Op_1);
  not not_4 (D__Op_0, D__Op_0);
  or or_1 (or_1_out, C__Op_1, D__Op_0);
  and and_1 (and_1_out, or_1_out, B__Op_2);
  // AND_Gate and_2 has open pins: out=branch
  // AND_Gate and_3 has open pins: out=jump
  // AND_Gate and_4 has open pins: out=bnzi
  // AND_Gate and_5 has open pins: out=store
  // AND_Gate and_6 has open pins: out=load
  // AND_Gate and_7 has open pins: out=hibrido
  // OR_Gate or_2 has open pins: out=write

  // Other names for the same wires on the sheet: A = A__Op_3; nA = A__Op_3; B = B__Op_2; nB = B__Op_2; C = C__Op_1;
  //   nC = C__Op_1; D = D__Op_0; nD = D__Op_0
endmodule
