// Logisim project NEW_dual_port_ram.circ as structural Verilog: 1 circuit, main circuit dual_port_ram
module dual_port_ram (
  input  [7:0] addr,
  input  [7:0] pc,
  input  [7:0] d,
  input  w,
  output [7:0] instr,
  output [7:0] data
);

  wire clock_1_out, or_1_out;
  wire [7:0] multiplexer_1_out;

  Clock clock_1 (.out(clock_1_out));
  or or_1 (or_1_out, w, clock_1_out);
  Multiplexer #(.width(8)) multiplexer_1 (.in0(addr), .in1(pc), .out(multiplexer_1_out), .sel(clock_1_out));
  RAM #(.asyncread("true")) ram_1 (
    .addr(multiplexer_1_out), .we(or_1_out), .oe(1'b1), .clk(clock_1_out), .din(d), .dout(data));
  Register #(.trigger("falling")) pcbuf (.D(data), .en(1'b1), .clk(clock_1_out), .Q(instr));  // open: clr
endmodule
