// Logisim project VLW.circ as structural Verilog: 20 circuits, main circuit main
module main (
);

  wire AddrSrc, AluSrc3, AluSrc4, Branch, Brzi, Clk, E, ImmSrc, Jump, MemRead, MemWrite, mov, MovH, MovL,
       RegWrite1, RegWrite3, RegWrite4;
  wire [2:0] AluOP3, AluOP4;
  wire [3:0] Imm1, Imm2, separador_instrucao_1_op1, separador_instrucao_1_op2, separador_instrucao_1_op3,
       separador_instrucao_1_op4, separador_instrucao_1_r1, separador_instrucao_1_r2,
       separador_instrucao_1_r3, separador_instrucao_1_r4;
  wire [7:0] A2, B2, banco_de_registradores_1_a1, banco_de_registradores_1_a3, banco_de_registradores_1_a4,
       banco_de_registradores_1_b1, banco_de_registradores_1_b3, banco_de_registradores_1_b4, Imm, Imm3,
       Imm4, mem_dados_1_s, mem_inst_1_s1, mem_inst_1_s2, mem_inst_1_s3, mem_inst_1_s4, move_1_s,
       multiplexer_1_out, multiplexer_2_out, R1, R3, R4;

  ExtSign extsign_1 (.Imm(Imm2), .Ext_Imm(Imm));
  PC_Src pc_src_1 (.D(A2), .Branch(Branch), .Jump(Jump), .S(E));
  mem_inst mem_inst_1 (
    .Imm(Imm), .Addr(B2), .ImmScr(ImmSrc), .AddrSrc(AddrSrc), .E(E), .Clk(Clk), .S1(mem_inst_1_s1),
    .S2(mem_inst_1_s2), .S3(mem_inst_1_s3), .S4(mem_inst_1_s4));
  Clock clock_1 (.out(Clk));
  Separador_Instrucao separador_instrucao_1 (
    .Instr1(mem_inst_1_s1), .Instr2(mem_inst_1_s2), .Instr3(mem_inst_1_s3), .Instr4(mem_inst_1_s4),
    .R1(separador_instrucao_1_r1), .R2(separador_instrucao_1_r2), .R3(separador_instrucao_1_r3),
    .R4(separador_instrucao_1_r4), .Imm1(Imm1), .Imm2(Imm2), .op1(separador_instrucao_1_op1),
    .op2(separador_instrucao_1_op2), .op3(separador_instrucao_1_op3), .op4(separador_instrucao_1_op4),
    .Imm3(Imm3), .Imm4(Imm4));
  Banco_de_Registradores banco_de_registradores_1 (
    .R1(separador_instrucao_1_r1), .R2(separador_instrucao_1_r2), .R3(separador_instrucao_1_r3),
    .R4(separador_instrucao_1_r4), .W1(R1), .W3(R3), .W4(R4), .RegWrite1(RegWrite1), .RegWrite3(RegWrite3),
    .RegWrite4(RegWrite4), .Move(mov), .brzi(Brzi), .Clk(Clk), .A1(banco_de_registradores_1_a1),
    .B1(banco_de_registradores_1_b1), .A2(A2), .B2(B2), .A3(banco_de_registradores_1_a3),
    .B3(banco_de_registradores_1_b3), .A4(banco_de_registradores_1_a4), .B4(banco_de_registradores_1_b4));
  Memoria_de_controle memoria_de_controle_1 (
    .opcode1(separador_instrucao_1_op1), .opcode2(separador_instrucao_1_op2),
    .opcode3(separador_instrucao_1_op3), .opcode4(separador_instrucao_1_op4), .MemRead(MemRead),
    .MemWrite(MemWrite), .MovH(MovH), .MovL(MovL), .Branch(Branch), .Jump(Jump), .AddrSrc(AddrSrc),
    .ImmSrc(ImmSrc), .AluOP3(AluOP3), .RegWrite3(RegWrite3), .AluSrc3(AluSrc3), .AluOP4(AluOP4),
    .RegWrite4(RegWrite4), .AluSrc4(AluSrc4));
  Multiplexer #(.width(8)) multiplexer_1 (
    .in0(banco_de_registradores_1_b3), .in1(Imm3), .out(multiplexer_1_out), .sel(AluSrc3));
  Multiplexer #(.width(8)) multiplexer_2 (
    .in0(banco_de_registradores_1_b4), .in1(Imm4), .out(multiplexer_2_out), .sel(AluSrc4));
  or or_1 (mov, MovH, MovL);
  Move move_1 (.E(banco_de_registradores_1_a1), .Imm(Imm1), .MovH(MovH), .MovL(MovL), .S(move_1_s));
  mem_dados mem_dados_1 (
    .Addr(banco_de_registradores_1_b1), .MemWrite(MemWrite), .MemRead(MemRead), .Clk(Clk),
    .D(banco_de_registradores_1_a1), .S(mem_dados_1_s));
  or or_2 (RegWrite1, mov, MemRead);
  and and_1 (Brzi, Branch, ImmSrc);
  Multiplexer #(.width(8)) multiplexer_3 (.in0(mem_dados_1_s), .in1(move_1_s), .out(R1), .sel(mov));
  ULA ula_1 (.A(banco_de_registradores_1_a3), .B(multiplexer_1_out), .AluOP(AluOP3), .C(R3));
  ULA ula_2 (.A(banco_de_registradores_1_a4), .B(multiplexer_2_out), .AluOP(AluOP4), .C(R4));
endmodule

module Banco_de_Registradores (
  input  [3:0] R1,
  input  [3:0] R2,
  input  [3:0] R3,
  input  [3:0] R4,
  input  [7:0] W1,
  input  [7:0] W3,
  input  [7:0] W4,
  input  RegWrite1,
  input  RegWrite3,
  input  RegWrite4,
  input  Move,
  input  brzi,
  input  Clk,
  output [7:0] A1,
  output [7:0] B1,
  output [7:0] A2,
  output [7:0] B2,
  output [7:0] A3,
  output [7:0] B3,
  output [7:0] A4,
  output [7:0] B4
);

  wire S10, S11, S12, S13, S30, S31, S32, S33, S40, S41, S42, S43;
  wire [1:0] multiplexer_5_out, multiplexer_22_out, multiplexer_23_out;
  wire [7:0] D0, D1, D2, D3, multiplexer_1_out, multiplexer_2_out, multiplexer_3_out, multiplexer_4_out,
       multiplexer_6_out, multiplexer_7_out, multiplexer_8_out, multiplexer_9_out, multiplexer_10_out,
       multiplexer_11_out, multiplexer_12_out, multiplexer_13_out;

  Multiplexer #(.width(8)) multiplexer_1 (.in0(D0), .in1(W1), .out(multiplexer_1_out), .sel(S10));
  Multiplexer #(.width(8)) multiplexer_2 (.in0(D1), .in1(W1), .out(multiplexer_2_out), .sel(S11));
  Multiplexer #(.width(8)) multiplexer_3 (.in0(D2), .in1(W1), .out(multiplexer_3_out), .sel(S12));
  Multiplexer #(.width(8)) multiplexer_4 (.in0(D3), .in1(W1), .out(multiplexer_4_out), .sel(S13));
  Multiplexer #(.width(2)) multiplexer_5 (.in0(R1[3:2]), .in1(2'b00), .out(multiplexer_5_out), .sel(Move));
  Multiplexer #(.width(8)) multiplexer_6 (.in0(multiplexer_1_out), .in1(W3), .out(multiplexer_6_out), .sel(S30));
  Multiplexer #(.width(8)) multiplexer_7 (.in0(multiplexer_2_out), .in1(W3), .out(multiplexer_7_out), .sel(S31));
  Multiplexer #(.width(8)) multiplexer_8 (.in0(multiplexer_3_out), .in1(W3), .out(multiplexer_8_out), .sel(S32));
  Multiplexer #(.width(8)) multiplexer_9 (.in0(multiplexer_4_out), .in1(W3), .out(multiplexer_9_out), .sel(S33));
  Demultiplexer #(.select(2)) demultiplexer_1 (
    .out0(S10), .out1(S11), .out2(S12), .out3(S13), .in(RegWrite1), .sel(multiplexer_5_out));
  Register register_1 (.D(multiplexer_10_out), .clk(Clk), .Q(D0));  // open: en, clr
  Multiplexer #(.width(8)) multiplexer_10 (.in0(multiplexer_6_out), .in1(W4), .out(multiplexer_10_out), .sel(S40));
  Register register_2 (.D(multiplexer_11_out), .clk(Clk), .Q(D1));  // open: en, clr
  Multiplexer #(.width(8)) multiplexer_11 (.in0(multiplexer_7_out), .in1(W4), .out(multiplexer_11_out), .sel(S41));
  Register register_3 (.D(multiplexer_12_out), .clk(Clk), .Q(D2));  // open: en, clr
  Multiplexer #(.width(8)) multiplexer_12 (.in0(multiplexer_8_out), .in1(W4), .out(multiplexer_12_out), .sel(S42));
  Register register_4 (.D(multiplexer_13_out), .clk(Clk), .Q(D3));  // open: en, clr
  Multiplexer #(.width(8)) multiplexer_13 (.in0(multiplexer_9_out), .in1(W4), .out(multiplexer_13_out), .sel(S43));
  Demultiplexer #(.select(2)) demultiplexer_2 (
    .out0(S30), .out1(S31), .out2(S32), .out3(S33), .in(RegWrite3), .sel(R3[3:2]));
  Multiplexer #(.select(2), .width(8)) multiplexer_14 (
    .in0(D0), .in1(D1), .in2(D2), .in3(D3), .out(A1), .sel(multiplexer_22_out));
  Multiplexer #(.select(2), .width(8)) multiplexer_15 (.in0(D0), .in1(D1), .in2(D2), .in3(D3), .out(B1), .sel(R1[1:0]));
  Multiplexer #(.select(2), .width(8)) multiplexer_16 (
    .in0(D0), .in1(D1), .in2(D2), .in3(D3), .out(A2), .sel(multiplexer_23_out));
  Multiplexer #(.select(2), .width(8)) multiplexer_17 (.in0(D0), .in1(D1), .in2(D2), .in3(D3), .out(B2), .sel(R2[1:0]));
  Multiplexer #(.select(2), .width(8)) multiplexer_18 (.in0(D0), .in1(D1), .in2(D2), .in3(D3), .out(A3), .sel(R3[3:2]));
  Multiplexer #(.select(2), .width(8)) multiplexer_19 (.in0(D0), .in1(D1), .in2(D2), .in3(D3), .out(B3), .sel(R3[1:0]));
  Multiplexer #(.select(2), .width(8)) multiplexer_20 (.in0(D0), .in1(D1), .in2(D2), .in3(D3), .out(A4), .sel(R4[3:2]));
  Multiplexer #(.select(2), .width(8)) multiplexer_21 (.in0(D0), .in1(D1), .in2(D2), .in3(D3), .out(B4), .sel(R4[1:0]));
  Demultiplexer #(.select(2)) demultiplexer_3 (
    .out0(S40), .out1(S41), .out2(S42), .out3(S43), .in(RegWrite4), .sel(R4[3:2]));
  Multiplexer #(.width(2)) multiplexer_22 (.in0(R1[3:2]), .in1(2'b00), .out(multiplexer_22_out), .sel(Move));
  Multiplexer #(.width(2)) multiplexer_23 (.in0(R2[3:2]), .in1(2'b00), .out(multiplexer_23_out), .sel(brzi));

  // Other names for the same wires on the sheet: B1_t[1:0] = R1[1:0]; A1_t[1:0] = R1[3:2]; B2_t[1:0] = R2[1:0];
  //   A2_t[1:0] = R2[3:2]; B3_t[1:0] = R3[1:0]; A3_t[1:0] = R3[3:2]; B4_t[1:0] = R4[1:0]; A4_t[1:0] = R4[3:2];
  //   RW1 = RegWrite1; RW3 = RegWrite3; RW4 = RegWrite4
endmodule

module ULA (
  input  [7:0] A,
  input  [7:0] B,
  input  [2:0] AluOP,
  output [7:0] C
);

  wire [7:0] op0, op1, op2, op3, op4, op5, op6, op7;

  op_add op_add_1 (.A(A), .B(B), .C(op0));
  op_sub op_sub_1 (.A(A), .B(B), .C(op1));
  op_not op_not_1 (.B(B), .C(op2));
  op_or op_or_1 (.A(A), .B(B), .C(op3));
  op_slr op_slr_1 (.A(A), .B(B), .C(op4));
  op_srr op_srr_1 (.A(A), .B(B), .C(op5));
  Multiplexer #(.select(3), .width(8)) multiplexer_1 (
    .in0(op0), .in1(op1), .in2(op2), .in3(op3), .in4(op4), .in5(op5), .in6(op6), .in7(op7), .out(C),
    .sel(AluOP));
endmodule

module ExtImm (
  input  [3:0] Imm,
  input  addie,
  input  Branch,
  output [7:0] Ext_Imm
);

  wire [7:0] adder_1_out, multiplexer_1_out, multiplexer_2_out;

  Multiplexer #(.width(8)) multiplexer_1 (.in0(8'h8), .in1(8'hf8), .out(multiplexer_1_out), .sel(Imm[3]));
  Adder adder_1 (.a({{5{Imm[3]}}, Imm[2:0]}), .b(multiplexer_1_out), .out(adder_1_out));  // open: cin, cout
  Multiplexer #(.width(8)) multiplexer_2 (
    .in0({{5{Imm[3]}}, Imm[2:0]}), .in1(adder_1_out), .out(multiplexer_2_out), .sel(addie));
  Multiplexer #(.width(8)) multiplexer_3 (.in0(multiplexer_2_out), .in1({8{1'b0}}), .out(Ext_Imm), .sel(Branch));
endmodule

module Separador_Instrucao (
  input  [7:0] Instr1,
  input  [7:0] Instr2,
  input  [7:0] Instr3,
  input  [7:0] Instr4,
  output [3:0] R1,
  output [3:0] R2,
  output [3:0] R3,
  output [3:0] R4,
  output [3:0] Imm1,
  output [3:0] Imm2,
  output [3:0] op1,
  output [3:0] op2,
  output [3:0] op3,
  output [3:0] op4,
  output [7:0] Imm3,
  output [7:0] Imm4
);

  wire not_1_out, not_2_out, not_3_out, sel1, sel2;

  Demultiplexer #(.width(4)) demultiplexer_1 (.out0(R1), .out1(Imm1), .in(Instr1[3:0]), .sel(sel1));
  Demultiplexer #(.width(4)) demultiplexer_2 (.out0(R2), .out1(Imm2), .in(Instr2[3:0]), .sel(sel2));
  ExtSingULA extsingula_1 (.Imm(Instr3[1:0]), .ExtSign(Imm3));
  ExtSingULA extsingula_2 (.Imm(Instr4[1:0]), .ExtSign(Imm4));
  and and_1 (sel1, Instr1[5], Instr1[6], not_1_out);
  not not_1 (not_1_out, Instr1[7]);
  not not_2 (not_2_out, Instr2[6]);
  and and_2 (sel2, Instr2[4], not_2_out, not_3_out);
  not not_3 (not_3_out, Instr2[7]);

  assign op1 = Instr1[7:4];
  assign op2 = Instr2[7:4];
  assign op3 = Instr3[7:4];
  assign op4 = Instr4[7:4];
  assign R3 = Instr3[3:0];
  assign R4 = Instr4[3:0];

  // Other names for the same wires on the sheet: X1[3:0] = Instr1[3:0]; X2[3:0] = Instr2[3:0];
  //   Imm3_t[3:0] = Instr3[3:0]; X3[3:0] = Instr3[3:0]; Imm4_t[3:0] = Instr4[3:0]; X4[3:0] = Instr4[3:0]
endmodule

module op_add (
  input  [7:0] A,
  input  [7:0] B,
  output [7:0] C
);

  Adder adder_1 (.a(A), .b(B), .out(C));  // open: cin, cout
endmodule

module op_sub (
  input  [7:0] A,
  input  [7:0] B,
  output [7:0] C
);

  Subtractor subtractor_1 (.a(A), .b(B), .out(C));  // open: bin, bout
endmodule

module op_and (
  input  [7:0] A,
  input  [7:0] B,
  output [7:0] C
);

  assign C = A & B;  // AND_Gate and_1, 8 bits wide
endmodule

module op_or (
  input  [7:0] A,
  input  [7:0] B,
  output [7:0] C
);

  assign C = A | B;  // OR_Gate or_1, 8 bits wide
endmodule

module op_xor (
  input  [7:0] A,
  input  [7:0] B,
  output [7:0] C
);

  assign C = A ^ B;  // XOR_Gate xor_1, 8 bits wide
endmodule

module op_slr (
  input  [7:0] A,
  input  [7:0] B,
  output [7:0] C
);

  wire or_1_out;
  wire [7:0] shifter_1_out;

  Shifter shifter_1 (.in(A), .\dist (B[2:0]), .out(shifter_1_out));
  Multiplexer #(.width(8)) multiplexer_1 (.in0(shifter_1_out), .in1({8{1'b0}}), .out(C), .sel(or_1_out));
  or or_1 (or_1_out, B[7], B[6], B[5], B[4], B[3]);
endmodule

module ExtSign (
  input  [3:0] Imm,
  output [7:0] Ext_Imm
);


  assign Ext_Imm = {{5{Imm[3]}}, Imm[2:0]};
endmodule

module Memoria_de_controle (
  input  [3:0] opcode1,
  input  [3:0] opcode2,
  input  [3:0] opcode3,
  input  [3:0] opcode4,
  output MemRead,
  output MemWrite,
  output MovH,
  output MovL,
  output Branch,
  output Jump,
  output AddrSrc,
  output ImmSrc,
  output [2:0] AluOP3,
  output RegWrite3,
  output AluSrc3,
  output [2:0] AluOP4,
  output RegWrite4,
  output AluSrc4
);

  wire and_4_out, and_5_out, and_6_out, and_7_out, and_10_out, and_11_out, and_14_out, and_15_out,
       and_17_out, and_18_out, and_19_out, and_20_out, nand_1_out, nand_2_out, not_1_out, not_2_out,
       not_3_out, not_4_out, not_5_out, not_6_out, not_7_out, not_8_out, not_9_out, not_10_out, not_11_out,
       not_12_out, not_13_out, not_14_out, not_15_out, not_16_out;

  not not_1 (not_1_out, opcode1[0]);
  not not_2 (not_2_out, opcode1[1]);
  not not_3 (not_3_out, opcode1[2]);
  not not_4 (not_4_out, opcode1[3]);
  and and_1 (MemRead, not_4_out, opcode1[2], not_2_out, not_1_out);
  not not_5 (not_5_out, opcode2[0]);
  not not_6 (not_6_out, opcode2[1]);
  not not_7 (not_7_out, opcode2[2]);
  not not_8 (not_8_out, opcode2[3]);
  and and_2 (Branch, not_6_out, not_7_out, not_8_out);
  not not_9 (not_9_out, opcode3[0]);
  not not_10 (not_10_out, opcode3[1]);
  not not_11 (not_11_out, opcode3[2]);
  not not_12 (not_12_out, opcode3[3]);
  not not_13 (not_13_out, opcode4[0]);
  not not_14 (not_14_out, opcode4[1]);
  not not_15 (not_15_out, opcode4[2]);
  not not_16 (not_16_out, opcode4[3]);
  and and_3 (Jump, opcode2[0], not_7_out, not_8_out);
  and and_4 (and_4_out, opcode3[3], not_11_out, not_10_out, opcode3[0]);
  and and_5 (and_5_out, opcode3[3], opcode3[2], opcode3[1], not_9_out);
  or or_1 (AluOP3[0], and_4_out, and_5_out);
  and and_6 (and_6_out, opcode4[3], not_15_out, not_14_out, opcode4[0]);
  and and_7 (and_7_out, opcode4[3], opcode4[2], opcode4[1], not_13_out);
  or or_2 (AluOP4[0], and_6_out, and_7_out);
  and and_8 (MemWrite, not_4_out, opcode1[2], not_2_out, opcode1[0]);
  and and_9 (AddrSrc, not_8_out, not_7_out, not_5_out);
  and and_10 (and_10_out, opcode3[3], not_11_out, opcode3[1], opcode3[0]);
  or or_3 (AluOP3[1], and_10_out, and_14_out);
  and and_11 (and_11_out, opcode4[3], not_15_out, opcode4[1], opcode4[0]);
  or or_4 (AluOP4[1], and_11_out, and_15_out);
  and and_12 (MovH, not_4_out, opcode1[2], opcode1[1], not_1_out);
  and and_13 (MovL, not_4_out, opcode1[2], opcode1[1], opcode1[0]);
  and and_14 (and_14_out, opcode3[3], opcode3[2], not_10_out, not_9_out);
  and and_15 (and_15_out, opcode4[3], opcode4[2], not_14_out, not_13_out);
  and and_16 (ImmSrc, not_8_out, not_7_out, opcode2[0]);
  and and_17 (and_17_out, opcode3[3], opcode3[2], not_10_out, opcode3[0]);
  and and_18 (and_18_out, opcode3[3], opcode3[2], opcode3[1], not_9_out);
  or or_5 (AluOP3[2], and_17_out, and_18_out);
  and and_19 (and_19_out, opcode4[3], opcode4[2], not_14_out, opcode4[0]);
  and and_20 (and_20_out, opcode4[3], opcode4[2], opcode4[1], not_13_out);
  or or_6 (AluOP4[2], and_19_out, and_20_out);
  and and_21 (RegWrite3, opcode3[3], nand_1_out);
  nand nand_1 (nand_1_out, opcode3[3], opcode3[2], opcode3[1], opcode3[0]);
  nand nand_2 (nand_2_out, opcode4[3], opcode4[2], opcode4[1], opcode4[0]);
  and and_22 (RegWrite4, opcode4[3], nand_2_out);
  and and_23 (AluSrc3, opcode3[3], not_11_out, opcode3[1], not_9_out);
  and and_24 (AluSrc4, opcode4[3], not_15_out, opcode4[1], not_13_out);

  // Other names for the same wires on the sheet: X0 = AluOP3[0]; X1 = AluOP3[1]; X2 = AluOP3[2]; Y0 = AluOP4[0];
  //   Y1 = AluOP4[1]; Y2 = AluOP4[2]
endmodule

module PC_Src (
  input  [7:0] D,
  input  Branch,
  input  Jump,
  output S
);

  wire and_1_out;
  wire [7:0] not_1_out;

  assign not_1_out = ~D;  // NOT_Gate not_1, 8 bits wide
  and and_1 (and_1_out, not_1_out[0], not_1_out[1], not_1_out[2], not_1_out[3], not_1_out[4], not_1_out[5], not_1_out[6], not_1_out[7], Branch);
  or or_1 (S, and_1_out, Jump);
endmodule

module op_not (
  input  [7:0] B,
  output [7:0] C
);

  wire or_1_out;

  Multiplexer #(.width(8)) multiplexer_1 (.in0(8'h1), .in1({8{1'b0}}), .out(C), .sel(or_1_out));
  or or_1 (or_1_out, B[7], B[6], B[5], B[4], B[3], B[2], B[1], B[0]);
endmodule

module op_srr (
  input  [7:0] A,
  input  [7:0] B,
  output [7:0] C
);

  wire or_1_out;
  wire [7:0] shifter_1_out;

  Shifter #(.shift("lr")) shifter_1 (.in(A), .\dist (B[2:0]), .out(shifter_1_out));
  Multiplexer #(.width(8)) multiplexer_1 (.in0(shifter_1_out), .in1({8{1'b0}}), .out(C), .sel(or_1_out));
  or or_1 (or_1_out, B[7], B[6], B[5], B[4], B[3]);
endmodule

module mem_inst (
  input  [7:0] Imm,
  input  [7:0] Addr,
  input  ImmScr,
  input  AddrSrc,
  input  E,
  input  Clk,
  output [7:0] S1,
  output [7:0] S2,
  output [7:0] S3,
  output [7:0] S4
);

  wire and_1_out, and_2_out;
  wire [7:0] adder_1_out, multiplexer_1_out, multiplexer_2_out, register_1_q;

  and and_1 (and_1_out, ImmScr, E);
  Adder adder_1 (.a(register_1_q), .b(multiplexer_1_out), .out(adder_1_out));  // open: cin, cout
  Multiplexer #(.width(8)) multiplexer_1 (.in0(8'h1), .in1(Imm), .out(multiplexer_1_out), .sel(and_1_out));
  Multiplexer #(.width(8)) multiplexer_2 (.in0(adder_1_out), .in1(Addr), .out(multiplexer_2_out), .sel(and_2_out));
  and and_2 (and_2_out, E, AddrSrc);
  Register register_1 (.D(multiplexer_2_out), .clk(Clk), .Q(register_1_q));  // open: en, clr
  ROM #(.dataWidth(32)) rom_1 (.addr(register_1_q), .data({S1, S2, S3, S4}));

  // Notes on the sheet:
  //   contents of rom_1 (hex, n*v repeats v):
  //   7fff9f9a 61ffad95 ffff88df 60ff86df 7bffff97 56ffffff 5012a6aa ff3effa3 7cffffff ffff848c ffffffa7
  //   41ff87ff 49ff87ff ffff88ff 591297ad ff3c97a7 ff30ffff
endmodule

module mem_dados (
  input  [7:0] Addr,
  input  MemWrite,
  input  MemRead,
  input  Clk,
  input  [7:0] D,
  output [7:0] S
);

  RAM #(.asyncread("true")) ram_1 (.addr(Addr), .we(MemWrite), .oe(MemRead), .clk(Clk), .din(D), .dout(S));
endmodule

module Move (
  input  [7:0] E,
  input  [3:0] Imm,
  input  MovH,
  input  MovL,
  output [7:0] S
);

  wire [3:0] multiplexer_1_out, multiplexer_2_out;

  Multiplexer #(.width(4)) multiplexer_1 (.in0(E[7:4]), .in1(Imm), .out(multiplexer_1_out), .sel(MovH));
  Multiplexer #(.width(4)) multiplexer_2 (.in0(E[3:0]), .in1(Imm), .out(multiplexer_2_out), .sel(MovL));
  Multiplexer #(.width(8)) multiplexer_3 (
    .in0({multiplexer_1_out, E[3:0]}), .in1({E[7:4], multiplexer_2_out}), .out(S), .sel(MovL));
endmodule

module ExtSingULA (
  input  [1:0] Imm,
  output [7:0] ExtSign
);


  assign ExtSign = {{7{Imm[1]}}, Imm[0]};
endmodule
